// Logisim project STDLGates.circ as structural Verilog: 15 circuits, main circuit NAND
module NAND (
  input  in_1,
  input  in_2,
  output out_3
);

  wire transistor_3_out;

  Transistor transistor_1 (.in(1'b1), .out(out_3), .gate(in_1));
  Transistor #(.\type ("n")) transistor_2 (.in(transistor_3_out), .out(out_3), .gate(in_1));
  Transistor #(.\type ("n")) transistor_3 (.in(1'b0), .out(transistor_3_out), .gate(in_2));
  Transistor transistor_4 (.in(1'b1), .out(out_3), .gate(in_2));
endmodule

module NOR (
  input  in_1,
  input  in_2,
  output out_3
);

  wire transistor_1_out;

  Transistor transistor_1 (.in(1'b1), .out(transistor_1_out), .gate(in_1));
  Transistor transistor_2 (.in(transistor_1_out), .out(out_3), .gate(in_2));
  Transistor #(.\type ("n")) transistor_3 (.in(1'b0), .out(out_3), .gate(in_2));
  Transistor #(.\type ("n")) transistor_4 (.in(1'b0), .out(out_3), .gate(in_1));
endmodule

module AND (
  input  in_1,
  input  in_2,
  output out_3
);

  wire nand_1_out_3;

  NAND nand_1 (.in_1(in_1), .in_2(in_2), .out_3(nand_1_out_3));
  NAND nand_2 (.in_1(nand_1_out_3), .in_2(nand_1_out_3), .out_3(out_3));
endmodule

module OR (
  input  in_1,
  input  in_2,
  output out_3
);

  wire nor_1_out_3;

  NOR nor_1 (.in_1(in_1), .in_2(in_2), .out_3(nor_1_out_3));
  NOR nor_2 (.in_1(nor_1_out_3), .in_2(nor_1_out_3), .out_3(out_3));
endmodule

module XOR (
  input  in_1,
  input  in_2,
  output out_3
);

  wire nand_1_out_3, nand_2_out_3, nand_3_out_3;

  NAND nand_1 (.in_1(in_1), .in_2(in_2), .out_3(nand_1_out_3));
  NAND nand_2 (.in_1(in_1), .in_2(nand_1_out_3), .out_3(nand_2_out_3));
  NAND nand_3 (.in_1(nand_1_out_3), .in_2(in_2), .out_3(nand_3_out_3));
  NAND nand_4 (.in_1(nand_2_out_3), .in_2(nand_3_out_3), .out_3(out_3));
endmodule

module XNOR (
  input  in_1,
  input  in_2,
  output out_3
);

  wire nor_1_out_3, nor_2_out_3, nor_3_out_3;

  NOR nor_1 (.in_1(in_1), .in_2(in_2), .out_3(nor_1_out_3));
  NOR nor_2 (.in_1(in_1), .in_2(nor_1_out_3), .out_3(nor_2_out_3));
  NOR nor_3 (.in_1(nor_1_out_3), .in_2(in_2), .out_3(nor_3_out_3));
  NOR nor_4 (.in_1(nor_2_out_3), .in_2(nor_3_out_3), .out_3(out_3));
endmodule

module NOT (
  input  in_1,
  output out_2
);

  Transistor transistor_1 (.in(1'b1), .out(out_2), .gate(in_1));
  Transistor #(.\type ("n")) transistor_2 (.in(1'b0), .out(out_2), .gate(in_1));
endmodule

module NAND16x2 (
  input  [15:0] in_1,
  input  [15:0] in_2,
  output [15:0] out_3
);

  NAND nand_1 (.in_1(in_1[0]), .in_2(in_2[0]), .out_3(out_3[0]));
  NAND nand_2 (.in_1(in_1[1]), .in_2(in_2[1]), .out_3(out_3[1]));
  NAND nand_3 (.in_1(in_1[2]), .in_2(in_2[2]), .out_3(out_3[2]));
  NAND nand_4 (.in_1(in_1[3]), .in_2(in_2[3]), .out_3(out_3[3]));
  NAND nand_5 (.in_1(in_1[4]), .in_2(in_2[4]), .out_3(out_3[4]));
  NAND nand_6 (.in_1(in_1[5]), .in_2(in_2[5]), .out_3(out_3[5]));
  NAND nand_7 (.in_1(in_1[6]), .in_2(in_2[6]), .out_3(out_3[6]));
  NAND nand_8 (.in_1(in_1[7]), .in_2(in_2[7]), .out_3(out_3[7]));
  NAND nand_9 (.in_1(in_1[8]), .in_2(in_2[8]), .out_3(out_3[8]));
  NAND nand_10 (.in_1(in_1[9]), .in_2(in_2[9]), .out_3(out_3[9]));
  NAND nand_11 (.in_1(in_1[10]), .in_2(in_2[10]), .out_3(out_3[10]));
  NAND nand_12 (.in_1(in_1[11]), .in_2(in_2[11]), .out_3(out_3[11]));
  NAND nand_13 (.in_1(in_1[12]), .in_2(in_2[12]), .out_3(out_3[12]));
  NAND nand_14 (.in_1(in_1[13]), .in_2(in_2[13]), .out_3(out_3[13]));
  NAND nand_15 (.in_1(in_1[14]), .in_2(in_2[14]), .out_3(out_3[14]));
  NAND nand_16 (.in_1(in_1[15]), .in_2(in_2[15]), .out_3(out_3[15]));
endmodule

module NOT16x2 (
  input  [15:0] in_1,
  input  [15:0] in_2,
  output [15:0] out_3
);

  NOT not_1 (.in_1(in_1[0]), .out_2(out_3[0]));
  NOT not_2 (.in_1(in_1[1]), .out_2(out_3[1]));
  NOT not_3 (.in_1(in_1[2]), .out_2(out_3[2]));
  NOT not_4 (.in_1(in_1[3]), .out_2(out_3[3]));
  NOT not_5 (.in_1(in_1[4]), .out_2(out_3[4]));
  NOT not_6 (.in_1(in_1[5]), .out_2(out_3[5]));
  NOT not_7 (.in_1(in_1[6]), .out_2(out_3[6]));
  NOT not_8 (.in_1(in_1[7]), .out_2(out_3[7]));
  NOT not_9 (.in_1(in_1[8]), .out_2(out_3[8]));
  NOT not_10 (.in_1(in_1[9]), .out_2(out_3[9]));
  NOT not_11 (.in_1(in_1[10]), .out_2(out_3[10]));
  NOT not_12 (.in_1(in_1[11]), .out_2(out_3[11]));
  NOT not_13 (.in_1(in_1[12]), .out_2(out_3[12]));
  NOT not_14 (.in_1(in_1[13]), .out_2(out_3[13]));
  NOT not_15 (.in_1(in_1[14]), .out_2(out_3[14]));
  NOT not_16 (.in_1(in_1[15]), .out_2(out_3[15]));
endmodule

module XNOR16x2 (
  input  [15:0] in_1,
  input  [15:0] in_2,
  output [15:0] out_3
);

  XNOR xnor_1 (.in_1(in_1[0]), .in_2(in_2[0]), .out_3(out_3[0]));
  XNOR xnor_2 (.in_1(in_1[1]), .in_2(in_2[1]), .out_3(out_3[1]));
  XNOR xnor_3 (.in_1(in_1[2]), .in_2(in_2[2]), .out_3(out_3[2]));
  XNOR xnor_4 (.in_1(in_1[3]), .in_2(in_2[3]), .out_3(out_3[3]));
  XNOR xnor_5 (.in_1(in_1[4]), .in_2(in_2[4]), .out_3(out_3[4]));
  XNOR xnor_6 (.in_1(in_1[5]), .in_2(in_2[5]), .out_3(out_3[5]));
  XNOR xnor_7 (.in_1(in_1[6]), .in_2(in_2[6]), .out_3(out_3[6]));
  XNOR xnor_8 (.in_1(in_1[7]), .in_2(in_2[7]), .out_3(out_3[7]));
  XNOR xnor_9 (.in_1(in_1[8]), .in_2(in_2[8]), .out_3(out_3[8]));
  XNOR xnor_10 (.in_1(in_1[9]), .in_2(in_2[9]), .out_3(out_3[9]));
  XNOR xnor_11 (.in_1(in_1[10]), .in_2(in_2[10]), .out_3(out_3[10]));
  XNOR xnor_12 (.in_1(in_1[11]), .in_2(in_2[11]), .out_3(out_3[11]));
  XNOR xnor_13 (.in_1(in_1[12]), .in_2(in_2[12]), .out_3(out_3[12]));
  XNOR xnor_14 (.in_1(in_1[13]), .in_2(in_2[13]), .out_3(out_3[13]));
  XNOR xnor_15 (.in_1(in_1[14]), .in_2(in_2[14]), .out_3(out_3[14]));
  XNOR xnor_16 (.in_1(in_1[15]), .in_2(in_2[15]), .out_3(out_3[15]));
endmodule

module XOR16x2 (
  input  [15:0] in_1,
  input  [15:0] in_2,
  output [15:0] out_3
);

  XOR xor_1 (.in_1(in_1[0]), .in_2(in_2[0]), .out_3(out_3[0]));
  XOR xor_2 (.in_1(in_1[1]), .in_2(in_2[1]), .out_3(out_3[1]));
  XOR xor_3 (.in_1(in_1[2]), .in_2(in_2[2]), .out_3(out_3[2]));
  XOR xor_4 (.in_1(in_1[3]), .in_2(in_2[3]), .out_3(out_3[3]));
  XOR xor_5 (.in_1(in_1[4]), .in_2(in_2[4]), .out_3(out_3[4]));
  XOR xor_6 (.in_1(in_1[5]), .in_2(in_2[5]), .out_3(out_3[5]));
  XOR xor_7 (.in_1(in_1[6]), .in_2(in_2[6]), .out_3(out_3[6]));
  XOR xor_8 (.in_1(in_1[7]), .in_2(in_2[7]), .out_3(out_3[7]));
  XOR xor_9 (.in_1(in_1[8]), .in_2(in_2[8]), .out_3(out_3[8]));
  XOR xor_10 (.in_1(in_1[9]), .in_2(in_2[9]), .out_3(out_3[9]));
  XOR xor_11 (.in_1(in_1[10]), .in_2(in_2[10]), .out_3(out_3[10]));
  XOR xor_12 (.in_1(in_1[11]), .in_2(in_2[11]), .out_3(out_3[11]));
  XOR xor_13 (.in_1(in_1[12]), .in_2(in_2[12]), .out_3(out_3[12]));
  XOR xor_14 (.in_1(in_1[13]), .in_2(in_2[13]), .out_3(out_3[13]));
  XOR xor_15 (.in_1(in_1[14]), .in_2(in_2[14]), .out_3(out_3[14]));
  XOR xor_16 (.in_1(in_1[15]), .in_2(in_2[15]), .out_3(out_3[15]));
endmodule

module OR16x2 (
  input  [15:0] in_1,
  input  [15:0] in_2,
  output [15:0] out_3
);

  OR or_1 (.in_1(in_1[0]), .in_2(in_2[0]), .out_3(out_3[0]));
  OR or_2 (.in_1(in_1[1]), .in_2(in_2[1]), .out_3(out_3[1]));
  OR or_3 (.in_1(in_1[2]), .in_2(in_2[2]), .out_3(out_3[2]));
  OR or_4 (.in_1(in_1[3]), .in_2(in_2[3]), .out_3(out_3[3]));
  OR or_5 (.in_1(in_1[4]), .in_2(in_2[4]), .out_3(out_3[4]));
  OR or_6 (.in_1(in_1[5]), .in_2(in_2[5]), .out_3(out_3[5]));
  OR or_7 (.in_1(in_1[6]), .in_2(in_2[6]), .out_3(out_3[6]));
  OR or_8 (.in_1(in_1[7]), .in_2(in_2[7]), .out_3(out_3[7]));
  OR or_9 (.in_1(in_1[8]), .in_2(in_2[8]), .out_3(out_3[8]));
  OR or_10 (.in_1(in_1[9]), .in_2(in_2[9]), .out_3(out_3[9]));
  OR or_11 (.in_1(in_1[10]), .in_2(in_2[10]), .out_3(out_3[10]));
  OR or_12 (.in_1(in_1[11]), .in_2(in_2[11]), .out_3(out_3[11]));
  OR or_13 (.in_1(in_1[12]), .in_2(in_2[12]), .out_3(out_3[12]));
  OR or_14 (.in_1(in_1[13]), .in_2(in_2[13]), .out_3(out_3[13]));
  OR or_15 (.in_1(in_1[14]), .in_2(in_2[14]), .out_3(out_3[14]));
  OR or_16 (.in_1(in_1[15]), .in_2(in_2[15]), .out_3(out_3[15]));
endmodule

module AND16x2 (
  input  [15:0] in_1,
  input  [15:0] in_2,
  output [15:0] out_3
);

  AND and_1 (.in_1(in_1[0]), .in_2(in_2[0]), .out_3(out_3[0]));
  AND and_2 (.in_1(in_1[1]), .in_2(in_2[1]), .out_3(out_3[1]));
  AND and_3 (.in_1(in_1[2]), .in_2(in_2[2]), .out_3(out_3[2]));
  AND and_4 (.in_1(in_1[3]), .in_2(in_2[3]), .out_3(out_3[3]));
  AND and_5 (.in_1(in_1[4]), .in_2(in_2[4]), .out_3(out_3[4]));
  AND and_6 (.in_1(in_1[5]), .in_2(in_2[5]), .out_3(out_3[5]));
  AND and_7 (.in_1(in_1[6]), .in_2(in_2[6]), .out_3(out_3[6]));
  AND and_8 (.in_1(in_1[7]), .in_2(in_2[7]), .out_3(out_3[7]));
  AND and_9 (.in_1(in_1[8]), .in_2(in_2[8]), .out_3(out_3[8]));
  AND and_10 (.in_1(in_1[9]), .in_2(in_2[9]), .out_3(out_3[9]));
  AND and_11 (.in_1(in_1[10]), .in_2(in_2[10]), .out_3(out_3[10]));
  AND and_12 (.in_1(in_1[11]), .in_2(in_2[11]), .out_3(out_3[11]));
  AND and_13 (.in_1(in_1[12]), .in_2(in_2[12]), .out_3(out_3[12]));
  AND and_14 (.in_1(in_1[13]), .in_2(in_2[13]), .out_3(out_3[13]));
  AND and_15 (.in_1(in_1[14]), .in_2(in_2[14]), .out_3(out_3[14]));
  AND and_16 (.in_1(in_1[15]), .in_2(in_2[15]), .out_3(out_3[15]));
endmodule

module NOR16x2 (
  input  [15:0] in_1,
  input  [15:0] in_2,
  output [15:0] out_3
);

  NOR nor_1 (.in_1(in_1[0]), .in_2(in_2[0]), .out_3(out_3[0]));
  NOR nor_2 (.in_1(in_1[1]), .in_2(in_2[1]), .out_3(out_3[1]));
  NOR nor_3 (.in_1(in_1[2]), .in_2(in_2[2]), .out_3(out_3[2]));
  NOR nor_4 (.in_1(in_1[3]), .in_2(in_2[3]), .out_3(out_3[3]));
  NOR nor_5 (.in_1(in_1[4]), .in_2(in_2[4]), .out_3(out_3[4]));
  NOR nor_6 (.in_1(in_1[5]), .in_2(in_2[5]), .out_3(out_3[5]));
  NOR nor_7 (.in_1(in_1[6]), .in_2(in_2[6]), .out_3(out_3[6]));
  NOR nor_8 (.in_1(in_1[7]), .in_2(in_2[7]), .out_3(out_3[7]));
  NOR nor_9 (.in_1(in_1[8]), .in_2(in_2[8]), .out_3(out_3[8]));
  NOR nor_10 (.in_1(in_1[9]), .in_2(in_2[9]), .out_3(out_3[9]));
  NOR nor_11 (.in_1(in_1[10]), .in_2(in_2[10]), .out_3(out_3[10]));
  NOR nor_12 (.in_1(in_1[11]), .in_2(in_2[11]), .out_3(out_3[11]));
  NOR nor_13 (.in_1(in_1[12]), .in_2(in_2[12]), .out_3(out_3[12]));
  NOR nor_14 (.in_1(in_1[13]), .in_2(in_2[13]), .out_3(out_3[13]));
  NOR nor_15 (.in_1(in_1[14]), .in_2(in_2[14]), .out_3(out_3[14]));
  NOR nor_16 (.in_1(in_1[15]), .in_2(in_2[15]), .out_3(out_3[15]));
endmodule

module test (
  input  in_1,
  output out_2
);

  Transistor transistor_1 (.in(1'b1), .out(out_2), .gate(in_1));
  Transistor #(.\type ("n")) transistor_2 (.in(1'b0), .out(out_2), .gate(in_1));
endmodule
