// Logisim project STDLMemory.circ as structural Verilog: 9 circuits, main circuit SRLatch
module SRLatch (
  input  S,
  input  Clock,
  input  R,
  output nQ,
  output Q
);

  wire and_1_out_3, and_2_out_3;

  AND and_1 (.in_1(S), .in_2(Clock), .out_3(and_1_out_3));
  AND and_2 (.in_1(Clock), .in_2(R), .out_3(and_2_out_3));
  NOR nor_1 (.in_1(and_1_out_3), .in_2(Q), .out_3(nQ));
  NOR nor_2 (.in_1(nQ), .in_2(and_2_out_3), .out_3(Q));
endmodule

module JKLatch (
  input  J,
  input  Clock,
  input  K,
  output nQ,
  output Q
);

  wire and_1_out_3, and_2_out_3, and_3_out_3, and_4_out_3;

  AND and_1 (.in_1(J), .in_2(Clock), .out_3(and_1_out_3));
  AND and_2 (.in_1(Clock), .in_2(K), .out_3(and_2_out_3));
  AND and_3 (.in_1(and_1_out_3), .in_2(nQ), .out_3(and_3_out_3));
  AND and_4 (.in_1(and_2_out_3), .in_2(Q), .out_3(and_4_out_3));
  NOR nor_1 (.in_1(and_3_out_3), .in_2(Q), .out_3(nQ));
  NOR nor_2 (.in_1(nQ), .in_2(and_4_out_3), .out_3(Q));
endmodule

module DLatch (
  input  D,
  input  Clock,
  output nQ,
  output Q
);

  wire not_1_out_2;

  NOT not_1 (.in_1(D), .out_2(not_1_out_2));
  SRLatch srlatch_1 (.S(D), .Clock(Clock), .R(not_1_out_2), .nQ(nQ), .Q(Q));
endmodule

module Register1 (
  input  D,
  input  Clock,
  output nQ,
  output Q
);

  DLatch dlatch_1 (.D(D), .Clock(Clock), .nQ(nQ), .Q(Q));
endmodule

module Register2 (
  input  [1:0] in_1,
  input  in_2,
  output [1:0] out_3,
  output [1:0] out_4
);

  Register1 _0 (.D(in_1[0]), .Clock(in_2), .nQ(out_3[0]), .Q(out_4[0]));
  Register1 _1 (.D(in_1[1]), .Clock(in_2), .nQ(out_3[1]), .Q(out_4[1]));
endmodule

module Register4 (
  input  [3:0] in_1,
  input  in_2,
  output [3:0] out_3,
  output [3:0] out_4
);

  Register2 register2_1 (.in_1(in_1[1:0]), .in_2(in_2), .out_3(out_3[1:0]), .out_4(out_4[1:0]));
  Register2 register2_2 (.in_1(in_1[3:2]), .in_2(in_2), .out_3(out_3[3:2]), .out_4(out_4[3:2]));
endmodule

module Register8 (
  input  [7:0] in_1,
  input  in_2,
  output [7:0] out_3,
  output [7:0] out_4
);

  Register4 register4_1 (.in_1(in_1[3:0]), .in_2(in_2), .out_3(out_3[3:0]), .out_4(out_4[3:0]));
  Register4 register4_2 (.in_1(in_1[7:4]), .in_2(in_2), .out_3(out_3[7:4]), .out_4(out_4[7:4]));
endmodule

module Register16 (
  input  [15:0] in_1,
  input  in_2,
  output [15:0] out_3,
  output [15:0] out_4
);

  Register8 register8_1 (.in_1(in_1[7:0]), .in_2(in_2), .out_3(out_3[7:0]), .out_4(out_4[7:0]));
  Register8 register8_2 (.in_1(in_1[15:8]), .in_2(in_2), .out_3(out_3[15:8]), .out_4(out_4[15:8]));
endmodule

module Register32 (
  input  [31:0] in_1,
  input  in_2,
  output [31:0] out_3,
  output [31:0] out_4
);

  Register16 register16_1 (.in_1(in_1[15:0]), .in_2(in_2), .out_3(out_3[15:0]), .out_4(out_4[15:0]));
  Register16 register16_2 (.in_1(in_1[31:16]), .in_2(in_2), .out_3(out_3[31:16]), .out_4(out_4[31:16]));
endmodule
