// Logisim project STDLPlexers.circ as structural Verilog
module Multiplexer1x2 (
  input  _0,
  input  _1,
  input  Select,
  output Output
);

  wire nand_1_out_3, nand_2_out_3, nand_3_out_3;

  NAND nand_1 (.in_1(Select), .in_2(Select), .out_3(nand_1_out_3));
  NAND nand_2 (.in_1(_1), .in_2(Select), .out_3(nand_2_out_3));
  NAND nand_3 (.in_1(nand_1_out_3), .in_2(_0), .out_3(nand_3_out_3));
  NAND nand_4 (.in_1(nand_2_out_3), .in_2(nand_3_out_3), .out_3(Output));
endmodule

module Multiplexer4x2 (
  input  [3:0] _0,
  input  [3:0] _1,
  input  in_3,
  output [3:0] out_4
);

  Multiplexer2x2 multiplexer2x2_1 (._0(_0[1:0]), ._1(_1[1:0]), .out_4(out_4[1:0]), .in_3(in_3));
  Multiplexer2x2 multiplexer2x2_2 (._0(_0[3:2]), ._1(_1[3:2]), .out_4(out_4[3:2]), .in_3(in_3));
endmodule

module Multiplexer2x2 (
  input  [1:0] _0,
  input  [1:0] _1,
  input  in_3,
  output [1:0] out_4
);

  Multiplexer1x2 multiplexer1x2_1 (._1(_1[0]), ._0(_0[0]), .Output(out_4[0]), .Select(in_3));
  Multiplexer1x2 multiplexer1x2_2 (._1(_1[1]), ._0(_0[1]), .Output(out_4[1]), .Select(in_3));
endmodule

module Multiplexer8x2 (
  input  [7:0] _0,
  input  [7:0] _1,
  input  in_3,
  output [7:0] out_4
);

  Multiplexer4x2 multiplexer4x2_1 (._0(_0[3:0]), ._1(_1[3:0]), .in_3(in_3), .out_4(out_4[3:0]));
  Multiplexer4x2 multiplexer4x2_2 (._0(_0[7:4]), ._1(_1[7:4]), .in_3(in_3), .out_4(out_4[7:4]));
endmodule

module Multiplexer16x2 (
  input  [15:0] _0,
  input  [15:0] _1,
  input  in_3,
  output [15:0] out_4
);

  Multiplexer8x2 multiplexer8x2_1 (._0(_0[7:0]), ._1(_1[7:0]), .in_3(in_3), .out_4(out_4[7:0]));
  Multiplexer8x2 multiplexer8x2_2 (._0(_0[15:8]), ._1(_1[15:8]), .in_3(in_3), .out_4(out_4[15:8]));
endmodule

module Multiplexer1x4 (
  input  _0,
  input  _1,
  input  _2,
  input  _3,
  input  [1:0] in_5,
  output out_6
);

  wire decoder2_1__1, decoder2_1__2, decoder2_1__3, multiplexer1x2_1_output, multiplexer1x2_2_output,
       or_1_out_3;

  Multiplexer1x2 multiplexer1x2_1 (._1(_1), ._0(_0), .Output(multiplexer1x2_1_output), .Select(decoder2_1__1));
  Multiplexer1x2 multiplexer1x2_2 (._1(_3), ._0(_2), .Output(multiplexer1x2_2_output), .Select(decoder2_1__3));
  Decoder2 decoder2_1 (
    .in_1(in_5), ._1(decoder2_1__1), ._2(decoder2_1__2), ._3(decoder2_1__3), .Enable(1'b1));  // open: _0
  Multiplexer1x2 multiplexer1x2_3 (
    ._1(multiplexer1x2_2_output), ._0(multiplexer1x2_1_output), .Output(out_6), .Select(or_1_out_3));
  OR or_1 (.in_1(decoder2_1__2), .in_2(decoder2_1__3), .out_3(or_1_out_3));
endmodule

module Decoder2 (
  input  [1:0] in_1,
  input  Enable,
  output _0,
  output _1,
  output _2,
  output _3
);

  wire not_1_out_2, not_2_out_2, not_3_out_2, not_4_out_2;
  wire [3:0] and_1_out_3;

  NOT not_1 (.in_1(in_1[0]), .out_2(not_1_out_2));
  AND and_1 (.in_1(not_1_out_2), .in_2(not_2_out_2), .out_3(and_1_out_3[0]));
  NOT not_2 (.in_1(in_1[1]), .out_2(not_2_out_2));
  AND and_2 (.in_1(in_1[0]), .in_2(not_3_out_2), .out_3(and_1_out_3[1]));
  NOT not_3 (.in_1(in_1[1]), .out_2(not_3_out_2));
  AND and_3 (.in_1(not_4_out_2), .in_2(in_1[1]), .out_3(and_1_out_3[2]));
  NOT not_4 (.in_1(in_1[0]), .out_2(not_4_out_2));
  AND and_4 (.in_1(in_1[0]), .in_2(in_1[1]), .out_3(and_1_out_3[3]));
  Multiplexer4x2 multiplexer4x2_1 (._0(4'b0000), ._1(and_1_out_3), .in_3(Enable), .out_4({_3, _2, _1, _0}));
endmodule

module Decoder3 (
  input  [2:0] in_1,
  input  Enable,
  output out_3,
  output out_4,
  output out_5,
  output out_6,
  output out_7,
  output out_8,
  output out_9,
  output out_10
);

  wire not_1_out_2;
  wire [7:0] decoder2_1__0;

  NOT not_1 (.in_1(in_1[2]), .out_2(not_1_out_2));
  Decoder2 decoder2_1 (
    .in_1(in_1[1:0]), ._0(decoder2_1__0[0]), ._1(decoder2_1__0[1]), ._2(decoder2_1__0[2]),
    ._3(decoder2_1__0[3]), .Enable(not_1_out_2));
  Decoder2 decoder2_2 (
    .in_1(in_1[1:0]), ._0(decoder2_1__0[4]), ._1(decoder2_1__0[5]), ._2(decoder2_1__0[6]),
    ._3(decoder2_1__0[7]), .Enable(in_1[2]));
  Multiplexer8x2 multiplexer8x2_1 (
    ._0({8{1'b0}}), ._1(decoder2_1__0), .in_3(Enable),
    .out_4({out_10, out_9, out_8, out_7, out_6, out_5, out_4, out_3}));
endmodule

module Decoder4 (
  input  [3:0] in_1,
  input  Enable,
  output out_3,
  output out_4,
  output out_5,
  output out_6,
  output out_7,
  output out_8,
  output out_9,
  output out_10,
  output out_11,
  output out_12,
  output out_13,
  output out_14,
  output out_15,
  output out_16,
  output out_17,
  output out_18
);

  wire not_1_out_2;
  wire [15:0] decoder3_1_out_3;

  NOT not_1 (.in_1(in_1[3]), .out_2(not_1_out_2));
  Decoder3 decoder3_1 (
    .in_1(in_1[2:0]), .out_3(decoder3_1_out_3[0]), .out_4(decoder3_1_out_3[1]), .out_5(decoder3_1_out_3[2]),
    .out_6(decoder3_1_out_3[3]), .out_7(decoder3_1_out_3[4]), .out_8(decoder3_1_out_3[5]),
    .out_9(decoder3_1_out_3[6]), .out_10(decoder3_1_out_3[7]), .Enable(not_1_out_2));
  Decoder3 decoder3_2 (
    .in_1(in_1[2:0]), .out_3(decoder3_1_out_3[8]), .out_4(decoder3_1_out_3[9]), .out_5(decoder3_1_out_3[10]),
    .out_6(decoder3_1_out_3[11]), .out_7(decoder3_1_out_3[12]), .out_8(decoder3_1_out_3[13]),
    .out_9(decoder3_1_out_3[14]), .out_10(decoder3_1_out_3[15]), .Enable(in_1[3]));
  Multiplexer16x2 multiplexer16x2_1 (
    ._0({16{1'b0}}), ._1(decoder3_1_out_3), .in_3(Enable),
    .out_4({out_18, out_17, out_16, out_15, out_14, out_13, out_12, out_11, out_10, out_9, out_8, out_7, out_6, out_5, out_4, out_3}));
endmodule

module Multiplexer2x4 (
  input  [1:0] _0,
  input  [1:0] _1,
  input  [1:0] _2,
  input  [1:0] _3,
  input  [1:0] in_5,
  output [1:0] out_6
);

  Multiplexer1x4 multiplexer1x4_1 (._0(_0[0]), ._1(_1[0]), ._2(_2[0]), ._3(_3[0]), .out_6(out_6[0]), .in_5(in_5));
  Multiplexer1x4 multiplexer1x4_2 (._0(_0[1]), ._1(_1[1]), ._2(_2[1]), ._3(_3[1]), .out_6(out_6[1]), .in_5(in_5));
endmodule

module Multiplexer4x4 (
  input  [3:0] _0,
  input  [3:0] _1,
  input  [3:0] _2,
  input  [3:0] _3,
  input  [1:0] in_5,
  output [3:0] out_6
);

  Multiplexer2x4 multiplexer2x4_1 (
    ._0(_0[1:0]), ._1(_1[1:0]), ._2(_2[1:0]), ._3(_3[1:0]), .out_6(out_6[1:0]), .in_5(in_5));
  Multiplexer2x4 multiplexer2x4_2 (
    ._0(_0[3:2]), ._1(_1[3:2]), ._2(_2[3:2]), ._3(_3[3:2]), .out_6(out_6[3:2]), .in_5(in_5));
endmodule

module Multiplexer8x4 (
  input  [7:0] in_1,
  input  [7:0] in_2,
  input  [7:0] in_3,
  input  [7:0] in_4,
  input  [1:0] in_5,
  output [7:0] out_6
);

  Multiplexer4x4 multiplexer4x4_1 (
    ._0(in_1[3:0]), ._1(in_2[3:0]), ._2(in_3[3:0]), ._3(in_4[3:0]), .out_6(out_6[3:0]), .in_5(in_5));
  Multiplexer4x4 multiplexer4x4_2 (
    ._0(in_1[7:4]), ._1(in_2[7:4]), ._2(in_3[7:4]), ._3(in_4[7:4]), .out_6(out_6[7:4]), .in_5(in_5));
endmodule

module Multiplexer16x4 (
  input  [15:0] in_1,
  input  [15:0] in_2,
  input  [15:0] in_3,
  input  [15:0] in_4,
  input  [1:0] in_5,
  output [15:0] out_6
);

  Multiplexer8x4 multiplexer8x4_1 (
    .in_1(in_1[7:0]), .in_2(in_2[7:0]), .in_3(in_3[7:0]), .in_4(in_4[7:0]), .out_6(out_6[7:0]), .in_5(in_5));
  Multiplexer8x4 multiplexer8x4_2 (
    .in_1(in_1[15:8]), .in_2(in_2[15:8]), .in_3(in_3[15:8]), .in_4(in_4[15:8]), .out_6(out_6[15:8]),
    .in_5(in_5));
endmodule

module Multiplexer1x8 (
  input  in_1,
  input  in_2,
  input  in_3,
  input  in_4,
  input  in_5,
  input  in_6,
  input  in_7,
  input  in_8,
  input  [2:0] in_9,
  output out_10
);

  wire multiplexer1x4_1_out_6, multiplexer1x4_2_out_6;

  Multiplexer1x4 multiplexer1x4_1 (
    ._0(in_1), ._1(in_2), ._2(in_3), ._3(in_4), .out_6(multiplexer1x4_1_out_6), .in_5(in_9[1:0]));
  Multiplexer1x4 multiplexer1x4_2 (
    ._0(in_5), ._1(in_6), ._2(in_7), ._3(in_8), .out_6(multiplexer1x4_2_out_6), .in_5(in_9[1:0]));
  Multiplexer1x2 multiplexer1x2_1 (
    ._1(multiplexer1x4_2_out_6), ._0(multiplexer1x4_1_out_6), .Output(out_10), .Select(in_9[2]));
endmodule

module Multiplexer2x8 (
  input  [1:0] in_1,
  input  [1:0] in_2,
  input  [1:0] in_3,
  input  [1:0] in_4,
  input  [1:0] in_5,
  input  [1:0] in_6,
  input  [1:0] in_7,
  input  [1:0] in_8,
  input  [2:0] in_9,
  output [1:0] out_10
);

  Multiplexer1x8 multiplexer1x8_1 (
    .in_1(in_1[0]), .in_2(in_2[0]), .in_3(in_3[0]), .in_4(in_4[0]), .in_5(in_5[0]), .in_6(in_6[0]),
    .in_7(in_7[0]), .in_8(in_8[0]), .out_10(out_10[0]), .in_9(in_9));
  Multiplexer1x8 multiplexer1x8_2 (
    .in_1(in_1[1]), .in_2(in_2[1]), .in_3(in_3[1]), .in_4(in_4[1]), .in_5(in_5[1]), .in_6(in_6[1]),
    .in_7(in_7[1]), .in_8(in_8[1]), .out_10(out_10[1]), .in_9(in_9));
endmodule

module Multiplexer4x8 (
  input  [3:0] in_1,
  input  [3:0] in_2,
  input  [3:0] in_3,
  input  [3:0] in_4,
  input  [3:0] in_5,
  input  [3:0] in_6,
  input  [3:0] in_7,
  input  [3:0] in_8,
  input  [2:0] in_9,
  output [3:0] out_10
);

  Multiplexer2x8 multiplexer2x8_1 (
    .in_1(in_1[1:0]), .in_2(in_2[1:0]), .in_3(in_3[1:0]), .in_4(in_4[1:0]), .in_5(in_5[1:0]),
    .in_6(in_6[1:0]), .in_7(in_7[1:0]), .in_8(in_8[1:0]), .out_10(out_10[1:0]), .in_9(in_9));
  Multiplexer2x8 multiplexer2x8_2 (
    .in_1(in_1[3:2]), .in_2(in_2[3:2]), .in_3(in_3[3:2]), .in_4(in_4[3:2]), .in_5(in_5[3:2]),
    .in_6(in_6[3:2]), .in_7(in_7[3:2]), .in_8(in_8[3:2]), .out_10(out_10[3:2]), .in_9(in_9));
endmodule

module Multiplexer8x8 (
  input  [7:0] in_1,
  input  [7:0] in_2,
  input  [7:0] in_3,
  input  [7:0] in_4,
  input  [7:0] in_5,
  input  [7:0] in_6,
  input  [7:0] in_7,
  input  [7:0] in_8,
  input  [2:0] in_9,
  output [7:0] out_10
);

  Multiplexer4x8 multiplexer4x8_1 (
    .in_1(in_1[3:0]), .in_2(in_2[3:0]), .in_3(in_3[3:0]), .in_4(in_4[3:0]), .in_5(in_5[3:0]),
    .in_6(in_6[3:0]), .in_7(in_7[3:0]), .in_8(in_8[3:0]), .out_10(out_10[3:0]), .in_9(in_9));
  Multiplexer4x8 multiplexer4x8_2 (
    .in_1(in_1[7:4]), .in_2(in_2[7:4]), .in_3(in_3[7:4]), .in_4(in_4[7:4]), .in_5(in_5[7:4]),
    .in_6(in_6[7:4]), .in_7(in_7[7:4]), .in_8(in_8[7:4]), .out_10(out_10[7:4]), .in_9(in_9));
endmodule

module Multiplexer16x8 (
  input  [15:0] in_1,
  input  [15:0] in_2,
  input  [15:0] in_3,
  input  [15:0] in_4,
  input  [15:0] in_5,
  input  [15:0] in_6,
  input  [15:0] in_7,
  input  [15:0] in_8,
  input  [2:0] in_9,
  output [15:0] out_10
);

  Multiplexer8x8 multiplexer8x8_1 (
    .in_1(in_1[7:0]), .in_2(in_2[7:0]), .in_3(in_3[7:0]), .in_4(in_4[7:0]), .in_5(in_5[7:0]),
    .in_6(in_6[7:0]), .in_7(in_7[7:0]), .in_8(in_8[7:0]), .out_10(out_10[7:0]), .in_9(in_9));
  Multiplexer8x8 multiplexer8x8_2 (
    .in_1(in_1[15:8]), .in_2(in_2[15:8]), .in_3(in_3[15:8]), .in_4(in_4[15:8]), .in_5(in_5[15:8]),
    .in_6(in_6[15:8]), .in_7(in_7[15:8]), .in_8(in_8[15:8]), .out_10(out_10[15:8]), .in_9(in_9));
endmodule

module Multiplexer1x16 (
  input  _0,
  input  _1,
  input  _2,
  input  _3,
  input  _4,
  input  _5,
  input  _6,
  input  _7,
  input  _8,
  input  _9,
  input  _10,
  input  _11,
  input  _12,
  input  _13,
  input  _14,
  input  _15,
  input  [3:0] in_17,
  output out_18
);

  wire multiplexer1x8_1_out_10, multiplexer1x8_2_out_10;

  Multiplexer1x8 multiplexer1x8_1 (
    .in_1(_0), .in_2(_1), .in_3(_2), .in_4(_3), .in_5(_4), .in_6(_5), .in_7(_6), .in_8(_7),
    .out_10(multiplexer1x8_1_out_10), .in_9(in_17[2:0]));
  Multiplexer1x8 multiplexer1x8_2 (
    .in_1(_8), .in_2(_9), .in_3(_10), .in_4(_11), .in_5(_12), .in_6(_13), .in_7(_14), .in_8(_15),
    .out_10(multiplexer1x8_2_out_10), .in_9(in_17[2:0]));
  Multiplexer1x2 multiplexer1x2_1 (
    ._1(multiplexer1x8_2_out_10), ._0(multiplexer1x8_1_out_10), .Output(out_18), .Select(in_17[3]));
endmodule

module Multiplexer2x16 (
  input  [1:0] _0,
  input  [1:0] _1,
  input  [1:0] _2,
  input  [1:0] _3,
  input  [1:0] _4,
  input  [1:0] _5,
  input  [1:0] _6,
  input  [1:0] _7,
  input  [1:0] _8,
  input  [1:0] _9,
  input  [1:0] _10,
  input  [1:0] _11,
  input  [1:0] _12,
  input  [1:0] _13,
  input  [1:0] _14,
  input  [1:0] _15,
  input  [3:0] in_17,
  output [1:0] out_18
);

  Multiplexer1x16 multiplexer1x16_1 (
    ._0(_0[0]), ._1(_1[0]), ._2(_2[0]), ._3(_3[0]), ._4(_4[0]), ._5(_5[0]), ._6(_6[0]), ._7(_7[0]),
    ._8(_8[0]), ._9(_9[0]), ._10(_10[0]), ._11(_11[0]), ._12(_12[0]), ._13(_13[0]), ._14(_14[0]),
    ._15(_15[0]), .out_18(out_18[0]), .in_17(in_17));
  Multiplexer1x16 multiplexer1x16_2 (
    ._0(_0[1]), ._1(_1[1]), ._2(_2[1]), ._3(_3[1]), ._4(_4[1]), ._5(_5[1]), ._6(_6[1]), ._7(_7[1]),
    ._8(_8[1]), ._9(_9[1]), ._10(_10[1]), ._11(_11[1]), ._12(_12[1]), ._13(_13[1]), ._14(_14[1]),
    ._15(_15[1]), .out_18(out_18[1]), .in_17(in_17));
endmodule

module Multiplexer4x16 (
  input  [3:0] _0,
  input  [3:0] _1,
  input  [3:0] _2,
  input  [3:0] _3,
  input  [3:0] _4,
  input  [3:0] _5,
  input  [3:0] _6,
  input  [3:0] _7,
  input  [3:0] _8,
  input  [3:0] _9,
  input  [3:0] _10,
  input  [3:0] _11,
  input  [3:0] _12,
  input  [3:0] _13,
  input  [3:0] _14,
  input  [3:0] _15,
  input  [3:0] in_17,
  output [3:0] out_18
);

  Multiplexer2x16 multiplexer2x16_1 (
    ._0(_0[1:0]), ._1(_1[1:0]), ._2(_2[1:0]), ._3(_3[1:0]), ._4(_4[1:0]), ._5(_5[1:0]), ._6(_6[1:0]),
    ._7(_7[1:0]), ._8(_8[1:0]), ._9(_9[1:0]), ._10(_10[1:0]), ._11(_11[1:0]), ._12(_12[1:0]), ._13(_13[1:0]),
    ._14(_14[1:0]), ._15(_15[1:0]), .out_18(out_18[1:0]), .in_17(in_17));
  Multiplexer2x16 multiplexer2x16_2 (
    ._0(_0[3:2]), ._1(_1[3:2]), ._2(_2[3:2]), ._3(_3[3:2]), ._4(_4[3:2]), ._5(_5[3:2]), ._6(_6[3:2]),
    ._7(_7[3:2]), ._8(_8[3:2]), ._9(_9[3:2]), ._10(_10[3:2]), ._11(_11[3:2]), ._12(_12[3:2]), ._13(_13[3:2]),
    ._14(_14[3:2]), ._15(_15[3:2]), .out_18(out_18[3:2]), .in_17(in_17));
endmodule

module Multiplexer8x16 (
  input  [7:0] _0,
  input  [7:0] _1,
  input  [7:0] _2,
  input  [7:0] _3,
  input  [7:0] _4,
  input  [7:0] _5,
  input  [7:0] _6,
  input  [7:0] _7,
  input  [7:0] _8,
  input  [7:0] _9,
  input  [7:0] _10,
  input  [7:0] _11,
  input  [7:0] _12,
  input  [7:0] _13,
  input  [7:0] _14,
  input  [7:0] _15,
  input  [3:0] in_17,
  output [7:0] out_18
);

  Multiplexer4x16 multiplexer4x16_1 (
    ._0(_0[3:0]), ._1(_1[3:0]), ._2(_2[3:0]), ._3(_3[3:0]), ._4(_4[3:0]), ._5(_5[3:0]), ._6(_6[3:0]),
    ._7(_7[3:0]), ._8(_8[3:0]), ._9(_9[3:0]), ._10(_10[3:0]), ._11(_11[3:0]), ._12(_12[3:0]), ._13(_13[3:0]),
    ._14(_14[3:0]), ._15(_15[3:0]), .out_18(out_18[3:0]), .in_17(in_17));
  Multiplexer4x16 multiplexer4x16_2 (
    ._0(_0[7:4]), ._1(_1[7:4]), ._2(_2[7:4]), ._3(_3[7:4]), ._4(_4[7:4]), ._5(_5[7:4]), ._6(_6[7:4]),
    ._7(_7[7:4]), ._8(_8[7:4]), ._9(_9[7:4]), ._10(_10[7:4]), ._11(_11[7:4]), ._12(_12[7:4]), ._13(_13[7:4]),
    ._14(_14[7:4]), ._15(_15[7:4]), .out_18(out_18[7:4]), .in_17(in_17));
endmodule

module Multiplexer16x16 (
  input  [15:0] _0,
  input  [15:0] _1,
  input  [15:0] _2,
  input  [15:0] _3,
  input  [15:0] _4,
  input  [15:0] _5,
  input  [15:0] _6,
  input  [15:0] _7,
  input  [15:0] _8,
  input  [15:0] _9,
  input  [15:0] _10,
  input  [15:0] _11,
  input  [15:0] _12,
  input  [15:0] _13,
  input  [15:0] _14,
  input  [15:0] _15,
  input  [3:0] in_17,
  output [15:0] out_18
);

  Multiplexer8x16 multiplexer8x16_1 (
    ._0(_0[7:0]), ._1(_1[7:0]), ._2(_2[7:0]), ._3(_3[7:0]), ._4(_4[7:0]), ._5(_5[7:0]), ._6(_6[7:0]),
    ._7(_7[7:0]), ._8(_8[7:0]), ._9(_9[7:0]), ._10(_10[7:0]), ._11(_11[7:0]), ._12(_12[7:0]), ._13(_13[7:0]),
    ._14(_14[7:0]), ._15(_15[7:0]), .out_18(out_18[7:0]), .in_17(in_17));
  Multiplexer8x16 multiplexer8x16_2 (
    ._0(_0[15:8]), ._1(_1[15:8]), ._2(_2[15:8]), ._3(_3[15:8]), ._4(_4[15:8]), ._5(_5[15:8]), ._6(_6[15:8]),
    ._7(_7[15:8]), ._8(_8[15:8]), ._9(_9[15:8]), ._10(_10[15:8]), ._11(_11[15:8]), ._12(_12[15:8]),
    ._13(_13[15:8]), ._14(_14[15:8]), ._15(_15[15:8]), .out_18(out_18[15:8]), .in_17(in_17));
endmodule
