// Logisim project test02.circ as structural Verilog: 2 circuits, main circuit main
module main (
  input  in_1,
  input  in_2,
  input  in_3,
  output out_4
);

  wire and_1_out, test02a_1_out_3, test02a_2_out_3;

  and and_1 (and_1_out, in_1, in_2);
  test02a test02a_1 (.in_1(and_1_out), .in_2(in_3), .out_3(test02a_1_out_3));
  test02a test02a_2 (.in_1(test02a_1_out_3), .in_2(test02a_1_out_3), .out_3(test02a_2_out_3));
  not not_1 (out_4, test02a_2_out_3);
endmodule

module test02a (
  input  in_1,
  input  in_2,
  output out_3
);

  wire not_1_out, not_2_out;

  not not_1 (not_1_out, in_1);
  not not_2 (not_2_out, in_2);
  or or_1 (out_3, not_1_out, not_2_out);
endmodule
