// Logisim project test03.circ as structural Verilog: 4 circuits, main circuit main
module main (
  input  in_1,
  input  in_2,
  input  in_3,
  output out_4
);

  wire test03a_1_out_3, test03a_2_out_3, test03b_1_out_3;

  test03b test03b_1 (.in_1(in_1), .in_2(in_2), .out_3(test03b_1_out_3));
  test03a test03a_1 (.in_1(test03b_1_out_3), .in_2(in_3), .out_3(test03a_1_out_3));
  test03a test03a_2 (.in_1(test03a_1_out_3), .in_2(test03a_1_out_3), .out_3(test03a_2_out_3));
  not not_1 (out_4, test03a_2_out_3);
endmodule

module test03a (
  input  in_1,
  input  in_2,
  output out_3
);

  or or_1 (out_3, in_1, in_2);
endmodule

module test03b (
  input  in_1,
  input  in_2,
  output out_3
);

  wire and_1_out, not_1_out;

  not not_1 (not_1_out, in_1);
  and and_1 (and_1_out, not_1_out, in_2);
  test03b1 test03b1_1 (.in_1(and_1_out), .out_2(out_3));
endmodule

module test03b1 (
  input  in_1,
  output out_2
);

  not not_1 (out_2, in_1);
endmodule
