// Logisim project test04.circ as structural Verilog
module main (
  input  in_1,
  output out_2
);

  test04c test04c_1 (.in_1(in_1), .out_2(out_2));
endmodule

module test04a (
  input  in_1,
  output out_2
);

  not not_1 (out_2, in_1);
endmodule

module test04c (
  input  in_1,
  output out_2
);

  not not_1 (out_2, in_1);
endmodule
