// Logisim project test05.circ as structural Verilog: 2 circuits, main circuit main
module main (
  input  in_1,
  output out_2
);

  not not_1 (out_2, in_1);
  test05a test05a_1 ();  // open: in_1, out_2

  // Notes on the sheet:
  //   Demonstrate failure to catch drawn but not connected circuits.
endmodule

module test05a (
  input  in_1,
  output out_2
);

  not not_1 (out_2, in_1);
endmodule
