// Logisim project 04-25) Parity.circ as structural Verilog: 1 circuit, main circuit main
module main (
  input  D1,
  input  D2,
  input  D3,
  input  D4,
  input  D1_2,
  input  D2_2,
  input  D3_2,
  input  D4_2,
  input  Parity_Bit,
  output D1_3,
  output D2_3,
  output D3_3,
  output D4_3,
  output Parity_Bit_2,
  output D1_4,
  output D2_4,
  output D3_4,
  output D4_4,
  output ERROR
);

  wire xor_1_out, xor_2_out, xor_3_out, xor_4_out, xor_6_out;

  xor xor_1 (xor_1_out, D4, D3);
  xor xor_2 (xor_2_out, D2, D1);
  xor xor_3 (xor_3_out, D4_2, D3_2);
  xor xor_4 (xor_4_out, D2_2, D1_2);
  xor xor_5 (Parity_Bit_2, xor_1_out, xor_2_out);
  xor xor_6 (xor_6_out, xor_3_out, xor_4_out);
  xor xor_7 (ERROR, Parity_Bit, xor_6_out);

  assign D1_3 = D1;
  assign D1_4 = D1_2;
  assign D2_3 = D2;
  assign D2_4 = D2_2;
  assign D3_3 = D3;
  assign D3_4 = D3_2;
  assign D4_3 = D4;
  assign D4_4 = D4_2;

  // Notes on the sheet:
  //   Even Parity Generator
  //   Even Parity Checker
endmodule
