// Logisim project 05-03) NAND Latch.circ as structural Verilog: 1 circuit, main circuit main
module main (
  input  SET,
  input  CLEAR,
  output Q,
  output nQ,
  output Q_2,
  output nQ_2,
  output Q_3,
  output nQ_3
);

  wire clear_out, not_1_out, not_2_out, pull_up_resistor_1_p1, pull_up_resistor_2_p1, set_out;

  not not_1 (not_1_out, set_out);
  Button u_set (.out(set_out));
  not not_2 (not_2_out, clear_out);
  Button u_clear (.out(clear_out));
  // Open_Push_Button set_2: pin names not known; wires that end beside it: 1'b0
  // Pull_up_Resistor pull_up_resistor_1: pin names not known; wires that end beside it: pull_up_resistor_1_p1
  // Open_Push_Button clear_2: pin names not known; wires that end beside it: 1'b0
  // Pull_up_Resistor pull_up_resistor_2: pin names not known; wires that end beside it: pull_up_resistor_2_p1
  nand nand_1 (Q, SET, nQ);
  nand nand_2 (nQ, Q, CLEAR);
  nand nand_3 (Q_2, not_1_out, nQ_2);
  nand nand_4 (nQ_2, Q_2, not_2_out);
  nand nand_5 (Q_3, pull_up_resistor_1_p1, nQ_3);
  nand nand_6 (nQ_3, Q_3, pull_up_resistor_2_p1);
endmodule
