// Logisim project 05-10) NOR Latch.circ as structural Verilog: 1 circuit, main circuit main
module main (
  input  CLEAR,
  input  SET,
  output Q,
  output nQ,
  output Q_2,
  output nQ_2,
  output Q_3,
  output nQ_3
);

  wire clear_out, pull_up_resistor_1_p1, pull_up_resistor_2_p1, set_out;

  Button u_clear (.out(clear_out));
  Button u_set (.out(set_out));
  // Pull_up_Resistor pull_up_resistor_1: pin names not known; wires that end beside it: pull_up_resistor_1_p1
  // Closed_Push_Button clear_2: pin names not known; wires that end beside it: 1'b0
  // Pull_up_Resistor pull_up_resistor_2: pin names not known; wires that end beside it: pull_up_resistor_2_p1
  // Closed_Push_Button set_2: pin names not known; wires that end beside it: 1'b0
  nor nor_1 (Q, CLEAR, nQ);
  nor nor_2 (nQ, Q, SET);
  nor nor_3 (Q_2, clear_out, nQ_2);
  nor nor_4 (nQ_2, Q_2, set_out);
  nor nor_5 (Q_3, pull_up_resistor_1_p1, nQ_3);
  nor nor_6 (nQ_3, Q_3, pull_up_resistor_2_p1);
endmodule
