// Logisim project 05-12) Burglar Alarm.circ as structural Verilog: 2 circuits, main circuit main
module main (
);

  wire nor_latch_1_q, photosensor_p2, reset_p2;

  // Closed_Push_Button photosensor: pin names not known; wires that end beside it: 1'b0, photosensor_p2
  // Closed_Push_Button reset: pin names not known; wires that end beside it: 1'b0, reset_p2
  // Pull_up_Resistor pull_up_resistor_1: pin names not known
  // Pull_up_Resistor pull_up_resistor_2: pin names not known
  NOR_Latch nor_latch_1 (.set(photosensor_p2), .clear(reset_p2), .Q(nor_latch_1_q));  // open: nQ
  // LED ALARM: pin names not known; wires that end beside it: nor_latch_1_q, 1'b0

  // Notes on the sheet:
  //   this switch represents a photosensor
  //   used to detect light
  //   if light is shining the switch should be closed
  //   open the switch if light is not shining
endmodule

module NOR_Latch (
  input  set,
  input  clear,
  output Q,
  output nQ
);

  nor nor_1 (nQ, set, Q);
  nor nor_2 (Q, nQ, clear);
endmodule
