// Logisim project 05-16) Clock Signals.circ as structural Verilog: 1 circuit, main circuit main
module main (
  output out_1
);

  Clock clock_1 (.out(out_1));

  // Notes on the sheet:
  //   Demonstrates a simple clock generator
  //   To see it work, you need to "Enable Ticks" under the Simulate menu
endmodule
