// Logisim project 05-21) S-C Flip-Flop.circ as structural Verilog: 4 circuits, main circuit S-C Flip-Flop
module S_C_Flip_Flop (
  input  set,
  input  clk,
  input  clear,
  output Q,
  output nQ
);

  wire edge_detector_1_clk_star, nand_1_out, nand_2_out;

  Edge_Detector edge_detector_1 (.clk(clk), .clk_star(edge_detector_1_clk_star));
  nand nand_1 (nand_1_out, set, edge_detector_1_clk_star);
  nand nand_2 (nand_2_out, edge_detector_1_clk_star, clear);
  NAND_Latch nand_latch_1 (.in_1(nand_1_out), .in_2(nand_2_out), .Q(Q), .nQ(nQ));
endmodule

module NAND_Latch (
  input  in_1,
  input  in_2,
  output Q,
  output nQ
);

  nand nand_1 (Q, in_1, nQ);
  nand nand_2 (nQ, Q, in_2);
endmodule

module Edge_Detector (
  input  clk,
  output clk_star
);

  wire not_1_out, not_2_out, not_3_out;

  not not_1 (not_1_out, not_3_out);
  not not_2 (not_2_out, clk);
  not not_3 (not_3_out, not_2_out);
  and and_1 (clk_star, clk, not_1_out);
endmodule

module S_C_Flip_Flop2 (
  input  set,
  input  clear,
  output Q,
  output nQ
);

  wire clk_out;

  Button clk (.out(clk_out));
  S_R_Flip_Flop s_r_ff_1 (.S(set), .clk(clk_out), .R(clear), .Q(Q), .Qn(nQ));  // open: preset, reset, en
endmodule
