// Logisim project 05-25) J-K Flip-Flop.circ as structural Verilog: 4 circuits, main circuit J-K Flip-Flop
module J_K_Flip_Flop (
  input  set,
  input  clk,
  input  clear,
  output Q,
  output nQ
);

  wire edge_detector_1_clk_star, nand_1_out, nand_2_out, startup_out;

  Edge_Detector edge_detector_1 (.clk(clk), .clk_star(edge_detector_1_clk_star));
  nand nand_1 (nand_1_out, set, nQ, edge_detector_1_clk_star);
  nand nand_2 (nand_2_out, edge_detector_1_clk_star, Q, clear);
  NAND_Latch nand_latch_1 (.in_1(nand_1_out), .in_2(nand_2_out), .Q(Q), .nQ(nQ), .start(startup_out));
  Button startup (.out(startup_out));

  // Notes on the sheet:
  //   Press the startup button to reset the circuit
endmodule

module NAND_Latch (
  input  in_1,
  input  in_2,
  input  start,
  output Q,
  output nQ
);

  wire multiplexer_1_out;

  Multiplexer multiplexer_1 (.in0(in_2), .in1(1'b0), .out(multiplexer_1_out), .sel(start));  // open: en
  nand nand_1 (Q, in_1, nQ);
  nand nand_2 (nQ, Q, multiplexer_1_out);
endmodule

module Edge_Detector (
  input  clk,
  output clk_star
);

  wire not_1_out, not_2_out, not_3_out;

  not not_1 (not_1_out, not_3_out);
  not not_2 (not_2_out, not_1_out);
  not not_3 (not_3_out, clk);
  and and_1 (clk_star, clk, not_2_out);
endmodule

module J_K_Flip_Flop2 (
  input  set,
  input  clear,
  output Q,
  output nQ
);

  wire clk_out;

  Button clk (.out(clk_out));
  J_K_Flip_Flop_part j_k_ff_1 (.J(set), .clk(clk_out), .K(clear), .Q(Q), .Qn(nQ));  // open: preset, en, reset
endmodule
