// Logisim project 05-27) D Flip-Flop.circ as structural Verilog: 2 circuits, main circuit D Flip-Flop
module D_Flip_Flop (
  input  data,
  output Q,
  output nQ
);

  wire clk_out, not_1_out;

  Button clk (.out(clk_out));
  not not_1 (not_1_out, data);
  J_K_Flip_Flop j_k_ff_1 (.J(data), .clk(clk_out), .K(not_1_out), .Q(Q), .Qn(nQ));  // open: preset, en, reset
endmodule

module D_Flip_Flop2 (
  input  data,
  output Q,
  output nQ
);

  wire clk_out;

  Button clk (.out(clk_out));
  D_Flip_Flop_part d_ff_1 (.clk(clk_out), .D(data), .Q(Q), .Qn(nQ));  // open: preset, en, reset
endmodule
