// Logisim project 05-28) Parallel Data Transfer.circ as structural Verilog: 1 circuit, main circuit Parallel Transfer
module Parallel_Transfer (
  input  D2,
  input  D1,
  input  D0,
  output Out2,
  output Out1,
  output Out0
);

  wire transfer_out;

  Button transfer (.out(transfer_out));
  D_Flip_Flop d_ff_1 (.clk(transfer_out), .D(D2), .Q(Out2));  // open: Qn, preset, en, reset
  D_Flip_Flop d_ff_2 (.clk(transfer_out), .D(D1), .Q(Out1));  // open: Qn, preset, en, reset
  D_Flip_Flop d_ff_3 (.clk(transfer_out), .D(D0), .Q(Out0));  // open: Qn, preset, en, reset
endmodule
