// Logisim project 05-29) D Latch.circ as structural Verilog: 1 circuit, main circuit D Latch
module D_Latch (
  input  enable,
  input  data,
  output Q,
  output nQ
);

  D_Flip_Flop #(.trigger("high")) d_ff_1 (.clk(enable), .D(data), .Q(Q), .Qn(nQ));  // open: preset, en, reset
endmodule
