// Logisim project 05-31) J-K Async Flip-Flop.circ as structural Verilog: 1 circuit, main circuit J-K Flip-Flop
module J_K_Flip_Flop (
  input  J,
  input  K,
  input  preset,
  input  clear,
  output Q,
  output nQ
);

  wire clk_out;

  Button clk (.out(clk_out));
  J_K_Flip_Flop_part j_k_ff_1 (
    .J(J), .clk(clk_out), .K(K), .Q(Q), .Qn(nQ), .preset(preset), .reset(clear));  // open: en
endmodule
