// Logisim project 05-38) Eliminating Partial Clock Pulses.circ as structural Verilog: 2 circuits, main circuit problem 
module problem (
  input  switch,
  output circuit_out,
  output clk_out
);

  Clock clk (.out(clk_out));
  and and_1 (circuit_out, switch, clk_out);

  // Notes on the sheet:
  //   Problem: The user can press button at any time - so the circuit out value may go HIGH after the clk out is already
  //   HIGH, or the circuit out value may go LOW before the clk out value goes LOW
endmodule

module fixed (
  input  switch,
  output circuit_out,
  output clk_out
);

  wire d_ff_1_q;

  Clock clk (.out(clk_out));
  D_Flip_Flop d_ff_1 (.clk(clk_out), .D(switch), .Q(d_ff_1_q));  // open: Qn, preset, en, reset
  and and_1 (circuit_out, d_ff_1_q, clk_out);

  // Notes on the sheet:
  //   Now, it's not possible for the circuit out value to be HIGH when the clk out value is not HIGH.
  //   Additionally, the circuit out value cannot go back to a LOW value until the clk out also goes to a LOW value.
endmodule
