// Logisim project 05-39) Detecting an Input Sequence.circ as structural Verilog: 1 circuit, main circuit main
module main (
  input  B,
  input  A,
  output X
);

  wire clear_out;

  D_Flip_Flop d_ff_1 (.clk(B), .D(A), .Q(X), .reset(clear_out));  // open: Qn, preset, en
  Button clear (.out(clear_out));

  // Notes on the sheet:
  //   Goal: ensure that A goes HIGH before B does
  //   This circuit outputs a HIGH value only if A goes HIGH before B does
endmodule
