// Logisim project 05-40) Synchronous Data Transfer.circ as structural Verilog: 2 circuits, main circuit transfer with J-K
module transfer_with_J_K (
  output Data_Currently_Being_Stored
);

  wire j_k_ff_1_q, j_k_ff_1_qn, Transfer_out;

  J_K_Flip_Flop j_k_ff_1 (.Q(j_k_ff_1_q), .Qn(j_k_ff_1_qn));  // open: J, clk, K, preset, en, reset
  // Probe on j_k_ff_1_q
  Button Transfer (.out(Transfer_out));
  J_K_Flip_Flop j_k_ff_2 (
    .J(j_k_ff_1_q), .clk(Transfer_out), .K(j_k_ff_1_qn), .Q(Data_Currently_Being_Stored), .preset(1'b0),
    .reset(1'b0));  // open: Qn, en
endmodule

module transfer_with_D (
  output Data_Currently_Being_Stored
);

  wire d_ff_1_q, Transfer_out;

  D_Flip_Flop d_ff_1 (.Q(d_ff_1_q));  // open: clk, D, Qn, preset, en, reset
  // Probe on d_ff_1_q
  Button Transfer (.out(Transfer_out));
  D_Flip_Flop d_ff_2 (
    .clk(Transfer_out), .D(d_ff_1_q), .Q(Data_Currently_Being_Stored), .preset(1'b0), .reset(1'b0));  // open: Qn, en
endmodule
