// Logisim project 05-41) Asynchronous Data Transfer.circ as structural Verilog: 1 circuit, main circuit transfer with J-K
module transfer_with_J_K (
  output Data_Currently_Being_Stored
);

  wire and_1_out, and_2_out, j_k_ff_1_q, j_k_ff_1_qn, Transfer_out;

  J_K_Flip_Flop j_k_ff_1 (.Q(j_k_ff_1_q), .Qn(j_k_ff_1_qn));  // open: J, clk, K, preset, en, reset
  // Probe on j_k_ff_1_q
  Button Transfer (.out(Transfer_out));
  and and_1 (and_1_out, j_k_ff_1_q, Transfer_out);
  J_K_Flip_Flop j_k_ff_2 (
    .J(1'b0), .clk(1'b0), .K(1'b0), .Q(Data_Currently_Being_Stored), .preset(and_1_out), .reset(and_2_out));  // open: Qn, en
  and and_2 (and_2_out, j_k_ff_1_qn, Transfer_out);
endmodule
