// Logisim project 05-42) 4-bit Parallel Data Transfer.circ as structural Verilog: 1 circuit, main circuit main
module main (
  output out_1,
  output out_2,
  output out_3,
  output out_4
);

  wire d_ff_1_q, d_ff_2_q, d_ff_3_q, d_ff_4_q, Transfer_out;

  D_Flip_Flop d_ff_1 (.Q(d_ff_1_q));  // open: clk, D, Qn, preset, en, reset
  D_Flip_Flop d_ff_2 (.Q(d_ff_2_q));  // open: clk, D, Qn, preset, en, reset
  D_Flip_Flop d_ff_3 (.Q(d_ff_3_q));  // open: clk, D, Qn, preset, en, reset
  D_Flip_Flop d_ff_4 (.Q(d_ff_4_q));  // open: clk, D, Qn, preset, en, reset
  Button Transfer (.out(Transfer_out));
  D_Flip_Flop d_ff_5 (.clk(Transfer_out), .D(d_ff_1_q), .Q(out_1));  // open: Qn, preset, en, reset
  D_Flip_Flop d_ff_6 (.clk(Transfer_out), .D(d_ff_2_q), .Q(out_2));  // open: Qn, preset, en, reset
  D_Flip_Flop d_ff_7 (.clk(Transfer_out), .D(d_ff_3_q), .Q(out_3));  // open: Qn, preset, en, reset
  D_Flip_Flop d_ff_8 (.clk(Transfer_out), .D(d_ff_4_q), .Q(out_4));  // open: Qn, preset, en, reset
endmodule
