// Logisim project 05-43) 4-bit Shift Register.circ as structural Verilog: 1 circuit, main circuit main
module main (
  input  Input_Data,
  output O3,
  output O2,
  output O1,
  output O0
);

  wire Shift_Pulses_out;

  Button Shift_Pulses (.out(Shift_Pulses_out));
  D_Flip_Flop d_ff_1 (.clk(Shift_Pulses_out), .D(Input_Data), .Q(O3));  // open: Qn, preset, en, reset
  D_Flip_Flop d_ff_2 (.clk(Shift_Pulses_out), .D(O3), .Q(O2));  // open: Qn, preset, en, reset
  D_Flip_Flop d_ff_3 (.clk(Shift_Pulses_out), .D(O2), .Q(O1));  // open: Qn, preset, en, reset
  D_Flip_Flop d_ff_4 (.clk(Shift_Pulses_out), .D(O1), .Q(O0));  // open: Qn, preset, en, reset

  // Notes on the sheet:
  //   (one bit at a time)
  //   Data Currently Being Stored
endmodule
