// Logisim project 05-44) Serial Data Transfer.circ as structural Verilog: 1 circuit, main circuit main
module main (
  output A2,
  output A1,
  output A0,
  output B2,
  output B1,
  output B0
);

  wire Shift_Pulses_out;

  Button Shift_Pulses (.out(Shift_Pulses_out));
  D_Flip_Flop d_ff_1 (.clk(Shift_Pulses_out), .Q(A2));  // open: D, Qn, preset, en, reset
  D_Flip_Flop d_ff_2 (.clk(Shift_Pulses_out), .D(A2), .Q(A1));  // open: Qn, preset, en, reset
  D_Flip_Flop d_ff_3 (.clk(Shift_Pulses_out), .D(A1), .Q(A0));  // open: Qn, preset, en, reset
  D_Flip_Flop d_ff_4 (.clk(Shift_Pulses_out), .D(A0), .Q(B2));  // open: Qn, preset, en, reset
  D_Flip_Flop d_ff_5 (.clk(Shift_Pulses_out), .D(B2), .Q(B1));  // open: Qn, preset, en, reset
  D_Flip_Flop d_ff_6 (.clk(Shift_Pulses_out), .D(B1), .Q(B0));  // open: Qn, preset, en, reset

  // Notes on the sheet:
  //   Data Currently Being Stored
endmodule
