// Logisim project 05-45) 3-bit Counter.circ as structural Verilog: 1 circuit, main circuit main
module main (
  output C,
  output B,
  output A
);

  wire clock_1_out;

  J_K_Flip_Flop #(.trigger("falling")) j_k_ff_1 (
    .J(1'b1), .clk(B), .K(1'b1), .Q(C), .preset(1'b0), .reset(1'b0));  // open: Qn, en
  J_K_Flip_Flop #(.trigger("falling")) j_k_ff_2 (
    .J(1'b1), .clk(A), .K(1'b1), .Q(B), .preset(1'b0), .reset(1'b0));  // open: Qn, en
  Clock clock_1 (.out(clock_1_out));
  J_K_Flip_Flop #(.trigger("falling")) j_k_ff_3 (
    .J(1'b1), .clk(clock_1_out), .K(1'b1), .Q(A), .preset(1'b0), .reset(1'b0));  // open: Qn, en
endmodule
