// Logisim project 05-48) Data Transfer using Addresses.circ as structural Verilog: 1 circuit, main circuit main
module main (
  input  A7,
  input  A6,
  input  A5,
  input  A4,
  input  A3,
  input  A2,
  input  A1,
  input  A0,
  input  WR,
  input  D3,
  input  D2,
  input  D1,
  input  D0
);

  wire and_1_out, and_2_out, not_1_out;

  not not_1 (not_1_out, A0);
  and and_1 (and_1_out, A7, A6, A5, A4, A3, A2, A1, not_1_out);
  and and_2 (and_2_out, and_1_out, WR);
  D_Flip_Flop d_ff_1 (.clk(and_2_out), .D(D3));  // open: Q, Qn, preset, en, reset
  D_Flip_Flop d_ff_2 (.clk(and_2_out), .D(D2));  // open: Q, Qn, preset, en, reset
  D_Flip_Flop d_ff_3 (.clk(and_2_out), .D(D1));  // open: Q, Qn, preset, en, reset
  D_Flip_Flop d_ff_4 (.clk(and_2_out), .D(D0));  // open: Q, Qn, preset, en, reset

  // Notes on the sheet:
  //   Address
  //   Data
  //   CPU
  //   4-bit Register
endmodule
