// Logisim project 06) Half Adder.circ as structural Verilog: 1 circuit, main circuit main
module main (
  input  A,
  input  B,
  output Cout,
  output Sum
);

  xor xor_1 (Sum, A, B);
  and and_1 (Cout, A, B);
endmodule
