// Logisim project 06-08a) 4-bit Full Adder.circ as structural Verilog: 1 circuit, main circuit main
module main (
  input  B3,
  input  B2,
  input  B1,
  input  B0,
  input  Cin,
  input  A3,
  input  A2,
  input  A1,
  input  A0,
  output Cout,
  output S3,
  output S2,
  output S1,
  output S0
);

  wire adder_2_cout, adder_3_cout, adder_4_cout;

  Adder #(.width(1)) adder_1 (.a(B3), .b(A3), .out(S3), .cin(adder_2_cout), .cout(Cout));
  Adder #(.width(1)) adder_2 (.a(B2), .b(A2), .out(S2), .cin(adder_3_cout), .cout(adder_2_cout));
  Adder #(.width(1)) adder_3 (.a(B1), .b(A1), .out(S1), .cin(adder_4_cout), .cout(adder_3_cout));
  Adder #(.width(1)) adder_4 (.a(B0), .b(A0), .out(S0), .cin(Cin), .cout(adder_4_cout));
endmodule
