// Logisim project 06-10) 4-bit Full Adder with Registers.circ as structural Verilog: 1 circuit, main circuit main
module main (
  input  in_1,
  input  in_2,
  input  in_3,
  input  in_4,
  input  Cin,
  output Cout,
  output S3,
  output S2,
  output S1,
  output S0
);

  wire adder_1_out, adder_2_cout, adder_2_out, adder_3_cout, adder_3_out, adder_4_cout, adder_4_out,
       Clear_out, d_ff_1_q, d_ff_3_q, d_ff_5_q, d_ff_7_q, Load_out, Transfer_out;

  Button Load (.out(Load_out));
  Button Transfer (.out(Transfer_out));
  Button Clear (.out(Clear_out));
  D_Flip_Flop d_ff_1 (.clk(Load_out), .D(in_1), .Q(d_ff_1_q), .preset(1'b0), .reset(1'b0));  // open: Qn, en
  D_Flip_Flop d_ff_2 (.clk(Transfer_out), .D(adder_1_out), .Q(S3), .preset(1'b0), .reset(Clear_out));  // open: Qn, en
  D_Flip_Flop d_ff_3 (.clk(Load_out), .D(in_2), .Q(d_ff_3_q), .preset(1'b0), .reset(1'b0));  // open: Qn, en
  Adder #(.width(1)) adder_1 (.a(d_ff_1_q), .b(S3), .out(adder_1_out), .cin(adder_2_cout), .cout(Cout));
  D_Flip_Flop d_ff_4 (.clk(Transfer_out), .D(adder_2_out), .Q(S2), .preset(1'b0), .reset(Clear_out));  // open: Qn, en
  Adder #(.width(1)) adder_2 (.a(d_ff_3_q), .b(S2), .out(adder_2_out), .cin(adder_3_cout), .cout(adder_2_cout));
  D_Flip_Flop d_ff_5 (.clk(Load_out), .D(in_3), .Q(d_ff_5_q), .preset(1'b0), .reset(1'b0));  // open: Qn, en
  Adder #(.width(1)) adder_3 (.a(d_ff_5_q), .b(S1), .out(adder_3_out), .cin(adder_4_cout), .cout(adder_3_cout));
  D_Flip_Flop d_ff_6 (.clk(Transfer_out), .D(adder_3_out), .Q(S1), .preset(1'b0), .reset(Clear_out));  // open: Qn, en
  D_Flip_Flop d_ff_7 (.clk(Load_out), .D(in_4), .Q(d_ff_7_q), .preset(1'b0), .reset(1'b0));  // open: Qn, en
  D_Flip_Flop d_ff_8 (.clk(Transfer_out), .D(adder_4_out), .Q(S0), .preset(1'b0), .reset(Clear_out));  // open: Qn, en
  Adder #(.width(1)) adder_4 (.a(d_ff_7_q), .b(S0), .out(adder_4_out), .cin(Cin), .cout(adder_4_cout));

  // Notes on the sheet:
  //   Memory
  //   B Register
  //   4-bit Adder
  //   A Register
endmodule
