// Logisim project 06-11a) 4-bit Full Adder Chip with Registers.circ as structural Verilog: 2 circuits, main circuit main
module main (
  input  in_1,
  input  in_2,
  input  in_3,
  input  in_4,
  input  Cin,
  output Cout,
  output S3,
  output S2,
  output S1,
  output S0
);

  wire Clear_out, d_ff_1_q, d_ff_3_q, d_ff_5_q, d_ff_7_q, Load_out, n74283_1_s0, n74283_1_s1, n74283_1_s2,
       n74283_1_s3, Transfer_out;

  Button Load (.out(Load_out));
  Button Transfer (.out(Transfer_out));
  Button Clear (.out(Clear_out));
  D_Flip_Flop d_ff_1 (.clk(Load_out), .D(in_1), .Q(d_ff_1_q), .preset(1'b0), .reset(1'b0));  // open: Qn, en
  D_Flip_Flop d_ff_2 (.clk(Transfer_out), .D(n74283_1_s3), .Q(S3), .preset(1'b0), .reset(Clear_out));  // open: Qn, en
  D_Flip_Flop d_ff_3 (.clk(Load_out), .D(in_2), .Q(d_ff_3_q), .preset(1'b0), .reset(1'b0));  // open: Qn, en
  D_Flip_Flop d_ff_4 (.clk(Transfer_out), .D(n74283_1_s2), .Q(S2), .preset(1'b0), .reset(Clear_out));  // open: Qn, en
  D_Flip_Flop d_ff_5 (.clk(Load_out), .D(in_3), .Q(d_ff_5_q), .preset(1'b0), .reset(1'b0));  // open: Qn, en
  _74283 u_74283_1 (
    .C4(Cout), .C0(Cin), .A3(d_ff_1_q), .A2(d_ff_3_q), .A1(d_ff_5_q), .A0(d_ff_7_q), .B3(S3), .B2(S2),
    .B1(S1), .B0(S0), .S3(n74283_1_s3), .S2(n74283_1_s2), .S1(n74283_1_s1), .S0(n74283_1_s0));
  D_Flip_Flop d_ff_6 (.clk(Transfer_out), .D(n74283_1_s1), .Q(S1), .preset(1'b0), .reset(Clear_out));  // open: Qn, en
  D_Flip_Flop d_ff_7 (.clk(Load_out), .D(in_4), .Q(d_ff_7_q), .preset(1'b0), .reset(1'b0));  // open: Qn, en
  D_Flip_Flop d_ff_8 (.clk(Transfer_out), .D(n74283_1_s0), .Q(S0), .preset(1'b0), .reset(Clear_out));  // open: Qn, en

  // Notes on the sheet:
  //   Memory
  //   B Register
  //   4-bit Adder
  //   A Register
endmodule

module _74283 (
  input  A3,
  input  A2,
  input  A1,
  input  A0,
  input  C0,
  input  B3,
  input  B2,
  input  B1,
  input  B0,
  output C4,
  output S3,
  output S2,
  output S1,
  output S0
);

  Adder #(.width(4)) adder_1 (.a({A3, A2, A1, A0}), .b({B3, B2, B1, B0}), .out({S3, S2, S1, S0}), .cin(C0), .cout(C4));
endmodule
