// Logisim project 06-11b) 8-bit Full Adder.circ as structural Verilog: 2 circuits, main circuit main
module main (
  input  A7,
  input  A6,
  input  A5,
  input  A4,
  input  A3,
  input  A2,
  input  A1,
  input  A0,
  input  Cin,
  input  B7,
  input  B6,
  input  B5,
  input  B4,
  input  B3,
  input  B2,
  input  B1,
  input  B0,
  output Cout,
  output S7,
  output S6,
  output S5,
  output S4,
  output S3,
  output S2,
  output S1,
  output S0
);

  wire n74283_2_c4;

  _74283 u_74283_1 (
    .C4(Cout), .C0(n74283_2_c4), .A3(A7), .A2(A6), .A1(A5), .A0(A4), .B3(B7), .B2(B6), .B1(B5), .B0(B4),
    .S3(S7), .S2(S6), .S1(S5), .S0(S4));
  _74283 u_74283_2 (
    .C4(n74283_2_c4), .C0(Cin), .A3(A3), .A2(A2), .A1(A1), .A0(A0), .B3(B3), .B2(B2), .B1(B1), .B0(B0),
    .S3(S3), .S2(S2), .S1(S1), .S0(S0));
endmodule

module _74283 (
  input  A3,
  input  A2,
  input  A1,
  input  A0,
  input  C0,
  input  B3,
  input  B2,
  input  B1,
  input  B0,
  output C4,
  output S3,
  output S2,
  output S1,
  output S0
);

  Adder #(.width(4)) adder_1 (.a({A3, A2, A1, A0}), .b({B3, B2, B1, B0}), .out({S3, S2, S1, S0}), .cin(C0), .cout(C4));
endmodule
