// Logisim project 06-12) Adder Configured to Subtract.circ as structural Verilog: 2 circuits, main circuit main
module main (
  input  A3,
  input  A2,
  input  A1,
  input  A0,
  input  B3,
  input  B2,
  input  B1,
  input  B0,
  output Cout,
  output S3,
  output S2,
  output S1,
  output S0
);

  wire not_1_out, not_2_out, not_3_out, not_4_out;

  _74283 u_74283_1 (
    .C4(Cout), .C0(1'b1), .A3(A3), .A2(A2), .A1(A1), .A0(A0), .B3(not_2_out), .B2(not_1_out), .B1(not_3_out),
    .B0(not_4_out), .S3(S3), .S2(S2), .S1(S1), .S0(S0));
  not not_1 (not_1_out, B2);
  not not_2 (not_2_out, B3);
  not not_3 (not_3_out, B1);
  not not_4 (not_4_out, B0);
endmodule

module _74283 (
  input  A3,
  input  A2,
  input  A1,
  input  A0,
  input  C0,
  input  B3,
  input  B2,
  input  B1,
  input  B0,
  output C4,
  output S3,
  output S2,
  output S1,
  output S0
);

  Adder #(.width(4)) adder_1 (.a({A3, A2, A1, A0}), .b({B3, B2, B1, B0}), .out({S3, S2, S1, S0}), .cin(C0), .cout(C4));
endmodule
