// Logisim project 06-14) 4-bit Parallel Adder-Subtracter with Regs.circ as structural Verilog: 2 circuits, main circuit main
module main (
  input  in_1,
  input  in_2,
  input  in_3,
  input  in_4,
  input  in_5,
  output Cout,
  output S3,
  output S2,
  output S1,
  output S0
);

  wire and_1_out, and_2_out, and_3_out, and_4_out, and_5_out, and_6_out, and_7_out, and_8_out, Clear_out,
       d_ff_1_q, d_ff_1_qn, d_ff_3_q, d_ff_3_qn, d_ff_5_q, d_ff_5_qn, d_ff_7_q, d_ff_7_qn, Load_out,
       n74283_1_s0, n74283_1_s1, n74283_1_s2, n74283_1_s3, not_1_out, or_1_out, or_2_out, or_3_out, or_4_out,
       Transfer_out;

  Button Load (.out(Load_out));
  not not_1 (not_1_out, in_5);
  Button Transfer (.out(Transfer_out));
  Button Clear (.out(Clear_out));
  D_Flip_Flop d_ff_1 (.clk(Load_out), .D(in_1), .Q(d_ff_1_q), .Qn(d_ff_1_qn), .preset(1'b0), .reset(1'b0));  // open: en
  and and_1 (and_1_out, in_5, d_ff_1_qn);
  or or_1 (or_1_out, and_1_out, and_2_out);
  D_Flip_Flop d_ff_2 (.clk(Transfer_out), .D(n74283_1_s3), .Q(S3), .preset(1'b0), .reset(Clear_out));  // open: Qn, en
  D_Flip_Flop d_ff_3 (.clk(Load_out), .D(in_2), .Q(d_ff_3_q), .Qn(d_ff_3_qn), .preset(1'b0), .reset(1'b0));  // open: en
  and and_2 (and_2_out, d_ff_1_q, not_1_out);
  and and_3 (and_3_out, in_5, d_ff_3_qn);
  D_Flip_Flop d_ff_4 (.clk(Transfer_out), .D(n74283_1_s2), .Q(S2), .preset(1'b0), .reset(Clear_out));  // open: Qn, en
  and and_4 (and_4_out, d_ff_3_q, not_1_out);
  or or_2 (or_2_out, and_3_out, and_4_out);
  D_Flip_Flop d_ff_5 (.clk(Load_out), .D(in_3), .Q(d_ff_5_q), .Qn(d_ff_5_qn), .preset(1'b0), .reset(1'b0));  // open: en
  and and_5 (and_5_out, d_ff_5_q, not_1_out);
  and and_6 (and_6_out, in_5, d_ff_5_qn);
  or or_3 (or_3_out, and_6_out, and_5_out);
  _74283 u_74283_1 (
    .C4(Cout), .C0(in_5), .A3(or_1_out), .A2(or_2_out), .A1(or_3_out), .A0(or_4_out), .B3(S3), .B2(S2),
    .B1(S1), .B0(S0), .S3(n74283_1_s3), .S2(n74283_1_s2), .S1(n74283_1_s1), .S0(n74283_1_s0));
  D_Flip_Flop d_ff_6 (.clk(Transfer_out), .D(n74283_1_s1), .Q(S1), .preset(1'b0), .reset(Clear_out));  // open: Qn, en
  D_Flip_Flop d_ff_7 (.clk(Load_out), .D(in_4), .Q(d_ff_7_q), .Qn(d_ff_7_qn), .preset(1'b0), .reset(1'b0));  // open: en
  and and_7 (and_7_out, d_ff_7_q, not_1_out);
  and and_8 (and_8_out, in_5, d_ff_7_qn);
  or or_4 (or_4_out, and_8_out, and_7_out);
  D_Flip_Flop d_ff_8 (.clk(Transfer_out), .D(n74283_1_s0), .Q(S0), .preset(1'b0), .reset(Clear_out));  // open: Qn, en

  // Notes on the sheet:
  //   0=add
  //   1=subtract
  //   Memory
  //   B Register
  //   4-bit Adder
  //   A Register
endmodule

module _74283 (
  input  A3,
  input  A2,
  input  A1,
  input  A0,
  input  C0,
  input  B3,
  input  B2,
  input  B1,
  input  B0,
  output C4,
  output S3,
  output S2,
  output S1,
  output S0
);

  Adder #(.width(4)) adder_1 (.a({A3, A2, A1, A0}), .b({B3, B2, B1, B0}), .out({S3, S2, S1, S0}), .cin(C0), .cout(C4));
endmodule
