// Logisim project 06-14a) BCD Adder.circ as structural Verilog: 2 circuits, main circuit main
module main (
  input  A3,
  input  A2,
  input  A1,
  input  A0,
  input  Carry_In,
  input  B3,
  input  B2,
  input  B1,
  input  B0,
  output Carry_Out,
  output S3,
  output S2,
  output S1,
  output S0
);

  wire and_1_out, n74283_2_c4, n74283_2_s0, n74283_2_s1, n74283_2_s2, n74283_2_s3, or_2_out;

  or or_1 (Carry_Out, n74283_2_c4, and_1_out);
  and and_1 (and_1_out, n74283_2_s3, or_2_out);
  or or_2 (or_2_out, n74283_2_s2, n74283_2_s1);
  _74283 u_74283_1 (
    .C0(1'b0), .A3(n74283_2_s3), .A2(n74283_2_s2), .A1(n74283_2_s1), .A0(n74283_2_s0), .B3(1'b0),
    .B2(Carry_Out), .B1(Carry_Out), .B0(1'b0), .S3(S3), .S2(S2), .S1(S1), .S0(S0));  // open: C4
  _74283 u_74283_2 (
    .C4(n74283_2_c4), .C0(Carry_In), .A3(A3), .A2(A2), .A1(A1), .A0(A0), .B3(B3), .B2(B2), .B1(B1), .B0(B0),
    .S3(n74283_2_s3), .S2(n74283_2_s2), .S1(n74283_2_s1), .S0(n74283_2_s0));

  // Notes on the sheet:
  //   CORRECTION
  //    MAIN
endmodule

module _74283 (
  input  A3,
  input  A2,
  input  A1,
  input  A0,
  input  C0,
  input  B3,
  input  B2,
  input  B1,
  input  B0,
  output C4,
  output S3,
  output S2,
  output S1,
  output S0
);

  Adder #(.width(4)) adder_1 (.a({A3, A2, A1, A0}), .b({B3, B2, B1, B0}), .out({S3, S2, S1, S0}), .cin(C0), .cout(C4));
endmodule
