// Logisim project 07-09) MOD-60 Counter.circ as structural Verilog: 1 circuit, main circuit main
module main (
  output F,
  output E,
  output D,
  output C,
  output B,
  output A
);

  wire and_1_out, clock_1_out;

  J_K_Flip_Flop #(.trigger("falling")) j_k_ff_1 (
    .J(1'b1), .clk(E), .K(1'b1), .Q(F), .preset(1'b0), .reset(and_1_out));  // open: Qn, en
  J_K_Flip_Flop #(.trigger("falling")) j_k_ff_2 (
    .J(1'b1), .clk(D), .K(1'b1), .Q(E), .preset(1'b0), .reset(and_1_out));  // open: Qn, en
  J_K_Flip_Flop #(.trigger("falling")) j_k_ff_3 (
    .J(1'b1), .clk(C), .K(1'b1), .Q(D), .preset(1'b0), .reset(and_1_out));  // open: Qn, en
  J_K_Flip_Flop #(.trigger("falling")) j_k_ff_4 (
    .J(1'b1), .clk(B), .K(1'b1), .Q(C), .preset(1'b0), .reset(and_1_out));  // open: Qn, en
  and and_1 (and_1_out, C, D, E, F);
  J_K_Flip_Flop #(.trigger("falling")) j_k_ff_5 (
    .J(1'b1), .clk(A), .K(1'b1), .Q(B), .preset(1'b0), .reset(and_1_out));  // open: Qn, en
  Clock clock_1 (.out(clock_1_out));
  J_K_Flip_Flop #(.trigger("falling")) j_k_ff_6 (
    .J(1'b1), .clk(clock_1_out), .K(1'b1), .Q(A), .preset(1'b0), .reset(and_1_out));  // open: Qn, en
endmodule
