// Logisim project 07-09a) 74293 Asynchronous Counter.circ as structural Verilog: 1 circuit, main circuit main
module main (
  input  CP0,
  input  CP1,
  input  MR0,
  input  MR1,
  output Q0,
  output Q1,
  output Q2,
  output Q3
);

  wire and_1_out;

  and and_1 (and_1_out, MR0, MR1);
  J_K_Flip_Flop #(.trigger("falling")) j_k_ff_1 (
    .J(1'b1), .clk(Q2), .K(1'b1), .Q(Q3), .preset(1'b0), .reset(and_1_out));  // open: Qn, en
  J_K_Flip_Flop #(.trigger("falling")) j_k_ff_2 (
    .J(1'b1), .clk(Q1), .K(1'b1), .Q(Q2), .preset(1'b0), .reset(and_1_out));  // open: Qn, en
  J_K_Flip_Flop #(.trigger("falling")) j_k_ff_3 (
    .J(1'b1), .clk(CP1), .K(1'b1), .Q(Q1), .preset(1'b0), .reset(and_1_out));  // open: Qn, en
  J_K_Flip_Flop #(.trigger("falling")) j_k_ff_4 (
    .J(1'b1), .clk(CP0), .K(1'b1), .Q(Q0), .preset(1'b0), .reset(and_1_out));  // open: Qn, en
endmodule
