// Logisim project 07-09b) 74293 Examples.circ as structural Verilog: 7 circuits, main circuit MOD-8
module MOD_8 (
  output out_1,
  output out_2,
  output out_3
);

  wire clock_1_out;

  Clock clock_1 (.out(clock_1_out));
  _74293 u_74293_1 (
    .CP0(1'b0), .CP1(clock_1_out), .MR0(1'b0), .MR1(1'b0), .Q1(out_3), .Q2(out_2), .Q3(out_1));  // open: Q0
endmodule

module MOD_16 (
  output out_1,
  output out_2,
  output out_3,
  output out_4
);

  wire clock_1_out;

  Clock clock_1 (.out(clock_1_out));
  _74293 u_74293_1 (
    .CP0(clock_1_out), .CP1(out_4), .MR0(1'b0), .MR1(1'b0), .Q0(out_4), .Q1(out_3), .Q2(out_2), .Q3(out_1));
endmodule

module MOD_10 (
  output out_1,
  output out_2,
  output out_3,
  output out_4
);

  wire clock_1_out;

  Clock clock_1 (.out(clock_1_out));
  _74293 u_74293_1 (
    .CP0(clock_1_out), .CP1(out_4), .MR0(out_3), .MR1(out_1), .Q0(out_4), .Q1(out_3), .Q2(out_2), .Q3(out_1));
endmodule

module MOD_14 (
  output out_1,
  output out_2,
  output out_3,
  output out_4
);

  wire and_1_out, clock_1_out;

  Clock clock_1 (.out(clock_1_out));
  and and_1 (and_1_out, out_2, out_3);
  _74293 u_74293_1 (
    .CP0(clock_1_out), .CP1(out_4), .MR0(and_1_out), .MR1(out_1), .Q0(out_4), .Q1(out_3), .Q2(out_2),
    .Q3(out_1));
endmodule

module MOD_60__a (
  output out_1,
  output out_2,
  output out_3,
  output out_4,
  output out_5,
  output out_6
);

  wire and_1_out, and_2_out, clock_1_out;

  _74293 u_74293_1 (.CP0(1'b0), .CP1(out_3), .MR0(and_2_out), .MR1(and_1_out), .Q1(out_2), .Q2(out_1));  // open: Q0, Q3
  and and_1 (and_1_out, out_2, out_1);
  Clock clock_1 (.out(clock_1_out));
  and and_2 (and_2_out, out_3, out_4);
  _74293 u_74293_2 (
    .CP0(clock_1_out), .CP1(out_6), .MR0(and_1_out), .MR1(and_2_out), .Q0(out_6), .Q1(out_5), .Q2(out_4),
    .Q3(out_3));

  // Notes on the sheet:
  //   Counts in proper counting sequence from 0-59
endmodule

module MOD_60__b (
  output out_1,
  output out_2,
  output out_3,
  output out_4,
  output out_5,
  output out_6,
  output out_7
);

  wire clock_1_out;

  _74293 u_74293_1 (.CP0(1'b0), .CP1(out_4), .MR0(out_2), .MR1(out_1), .Q1(out_3), .Q2(out_2), .Q3(out_1));  // open: Q0
  Clock clock_1 (.out(clock_1_out));
  _74293 u_74293_2 (
    .CP0(clock_1_out), .CP1(out_7), .MR0(out_6), .MR1(out_4), .Q0(out_7), .Q1(out_6), .Q2(out_5), .Q3(out_4));

  // Notes on the sheet:
  //   Counts through 60 states, but NOT in order from 0-59
endmodule

module _74293 (
  input  CP0,
  input  CP1,
  input  MR0,
  input  MR1,
  output Q0,
  output Q1,
  output Q2,
  output Q3
);

  wire and_1_out;

  and and_1 (and_1_out, MR0, MR1);
  J_K_Flip_Flop #(.trigger("falling")) j_k_ff_1 (
    .J(1'b1), .clk(Q2), .K(1'b1), .Q(Q3), .preset(1'b0), .reset(and_1_out));  // open: Qn, en
  J_K_Flip_Flop #(.trigger("falling")) j_k_ff_2 (
    .J(1'b1), .clk(Q1), .K(1'b1), .Q(Q2), .preset(1'b0), .reset(and_1_out));  // open: Qn, en
  J_K_Flip_Flop #(.trigger("falling")) j_k_ff_3 (
    .J(1'b1), .clk(CP1), .K(1'b1), .Q(Q1), .preset(1'b0), .reset(and_1_out));  // open: Qn, en
  J_K_Flip_Flop #(.trigger("falling")) j_k_ff_4 (
    .J(1'b1), .clk(CP0), .K(1'b1), .Q(Q0), .preset(1'b0), .reset(and_1_out));  // open: Qn, en
endmodule
