// Logisim project 07-10) 3-bit Down Counter.circ as structural Verilog: 1 circuit, main circuit main
module main (
  output C,
  output B,
  output A
);

  wire clock_1_out, j_k_ff_2_qn, j_k_ff_3_qn;

  J_K_Flip_Flop #(.trigger("falling")) j_k_ff_1 (
    .J(1'b1), .clk(j_k_ff_2_qn), .K(1'b1), .Q(C), .preset(1'b0), .reset(1'b0));  // open: Qn, en
  J_K_Flip_Flop #(.trigger("falling")) j_k_ff_2 (
    .J(1'b1), .clk(j_k_ff_3_qn), .K(1'b1), .Q(B), .Qn(j_k_ff_2_qn), .preset(1'b0), .reset(1'b0));  // open: en
  Clock clock_1 (.out(clock_1_out));
  J_K_Flip_Flop #(.trigger("falling")) j_k_ff_3 (
    .J(1'b1), .clk(clock_1_out), .K(1'b1), .Q(A), .Qn(j_k_ff_3_qn), .preset(1'b0), .reset(1'b0));  // open: en
endmodule
