// Logisim project 07-10a) Propagation Delay in Counters.circ as structural Verilog: 1 circuit, main circuit main
module main (
  output C,
  output B,
  output A
);

  wire and_1_out, and_2_out, and_3_out, clear_2_out, clear_3_out, clear_out, clock_1_out;

  Clock clock_1 (.out(clock_1_out));
  and and_1 (and_1_out, C, ~B, ~A);  // AND_Gate
  J_K_Flip_Flop #(.trigger("falling")) j_k_ff_1 (
    .J(1'b1), .clk(B), .K(1'b1), .Q(C), .preset(1'b0), .reset(1'b0));  // open: Qn, en
  D_Flip_Flop d_ff_1 (.preset(and_1_out), .reset(clear_out));  // open: clk, D, Q, Qn, en
  Button clear (.out(clear_out));
  J_K_Flip_Flop #(.trigger("falling")) j_k_ff_2 (
    .J(1'b1), .clk(A), .K(1'b1), .Q(B), .preset(1'b0), .reset(1'b0));  // open: Qn, en
  and and_2 (and_2_out, ~C, B, ~A);  // AND_Gate
  Button clear_2 (.out(clear_2_out));
  D_Flip_Flop d_ff_2 (.preset(and_2_out), .reset(clear_2_out));  // open: clk, D, Q, Qn, en
  J_K_Flip_Flop #(.trigger("falling")) j_k_ff_3 (
    .J(1'b1), .clk(clock_1_out), .K(1'b1), .Q(A), .preset(1'b0), .reset(1'b0));  // open: Qn, en
  and and_3 (and_3_out, ~C, ~B, ~A);  // AND_Gate
  D_Flip_Flop d_ff_3 (.preset(and_3_out), .reset(clear_3_out));  // open: clk, D, Q, Qn, en
  Button clear_3 (.out(clear_3_out));

  // Notes on the sheet:
  //   Counter in state 4
  //   Counter in state 2
  //   Counter in state 0
endmodule
