// Logisim project 07-10b) Synchronous 4-bit Counter.circ as structural Verilog: 1 circuit, main circuit main
module main (
  output D,
  output C,
  output B,
  output A
);

  wire and_1_out, and_2_out, clock_1_out;

  and and_1 (and_1_out, C, B, A);
  Clock clock_1 (.out(clock_1_out));
  J_K_Flip_Flop j_k_ff_1 (
    .J(and_1_out), .clk(clock_1_out), .K(and_1_out), .Q(D), .preset(1'b0), .reset(1'b0));  // open: Qn, en
  and and_2 (and_2_out, B, A);
  J_K_Flip_Flop j_k_ff_2 (
    .J(and_2_out), .clk(clock_1_out), .K(and_2_out), .Q(C), .preset(1'b0), .reset(1'b0));  // open: Qn, en
  J_K_Flip_Flop j_k_ff_3 (.J(A), .clk(clock_1_out), .K(A), .Q(B), .preset(1'b0), .reset(1'b0));  // open: Qn, en
  J_K_Flip_Flop j_k_ff_4 (.J(1'b1), .clk(clock_1_out), .K(1'b1), .Q(A), .preset(1'b0), .reset(1'b0));  // open: Qn, en

  // Notes on the sheet:
  //   Note: This AND gate is not connected
  //   to the output of the (A*B) and gate to
  //   avoid the propagation delay of
  //   another AND gate
  //   Total propagation delay = (FF delay) + (AND gate delay)
endmodule
